# Fritzing sketch Aquário Conectado (saved by Fritzing 0.9.3b)
circuit board: 8.46667cm x 5.64444cm
breadboards: 1

parts:
  Q1 = TIP120 Hi-Current Darlington Transistor
  Q2 = TIP120 Hi-Current Darlington Transistor
  Q3 = TIP120 Hi-Current Darlington Transistor
  R1 = Resistor [tolerance=±5% resistance=470 package=THT]
  R2 = Resistor [tolerance=±5% resistance=470 package=THT]
  R3 = Resistor [tolerance=±5% resistance=470 package=THT]
  R5 = Resistor [tolerance=±5% resistance=1k package=THT]
  D4 = Rectifier Diode [part_number=1N4001 package="300 mil [THT]"]
  12V = Screw terminal - 2 pins [package=THT]
  C2 = Electrolytic Capacitor [capacitance=10µF package="100 mil [THT, electrolytic]"]
  C3 = Electrolytic Capacitor [capacitance=22µF package="100 mil [THT, electrolytic]"]
  R6 = Resistor [tolerance=±5% resistance=4.7k package=THT]
  Relay1 = screw terminal, 2 pins
  Relay2 = screw terminal, 2 pins
  R7 = Resistor [tolerance=±5% resistance=1k package=THT]
  D5 = Rectifier Diode [part_number=1N4001 package="300 mil [THT]"]
  U10 = Voltage Regulator - 5V [package="TO220 [THT]"]
  C4 = Electrolytic Capacitor [capacitance=10µF package="100 mil [THT, electrolytic]"]
  C5 = Electrolytic Capacitor [capacitance=10µF package="100 mil [THT, electrolytic]"]
  WiFi-Witty-Gizwits-ESP-12F1 = WiFi-Witty-Gizwits-ESP-12F
  Q5 = NPN-Transistor [package="TO92 [THT]"]
  Q6 = NPN-Transistor [package="TO92 [THT]"]
  K1 = OMRON PCB Power Relay – G5LE [part_number="G5LE-1\n" package=THT]
  K2 = OMRON PCB Power Relay – G5LE [part_number="G5LE-1\n" package=THT]
  Q7 = NPN-Transistor [package="TO92 [THT]"]
  R8 = Resistor [tolerance=±5% resistance=1k package=THT]
  J1 = female pin header, 4 pins [form="♀ (female)"]
  5V_GND_RGB_LED_e_Racão = screw terminal, 6 pins
  DS18B20_e_PIR = screw terminal, 3 pins
  IC1 = Voltage Regulator AMS1117 [package=sot223]

nets:
  N1: Q1.BASE, R1.Pin_1
  N2: Q1.COLLECTOR, 5V_GND_RGB_LED_e_Racão.pin4
  GND: Q1.EMITTER, Q2.EMITTER, Q3.EMITTER, 12V.pin1, C2.-, C3.-, U10.GND, C4.-, C5.-, WiFi-Witty-Gizwits-ESP-12F1.GND, Q5.E, Q6.E, Q7.E, J1.pin1, 5V_GND_RGB_LED_e_Racão.pin5, IC1.GND
  N3: Q2.BASE, R2.Pin_1
  N4: Q2.COLLECTOR, 5V_GND_RGB_LED_e_Racão.pin3
  N5: Q3.BASE, R3.Pin_1
  N6: Q3.COLLECTOR, 5V_GND_RGB_LED_e_Racão.pin2
  N7: R1.Pin_0, WiFi-Witty-Gizwits-ESP-12F1.GPIO5
  N8: R2.Pin_0, WiFi-Witty-Gizwits-ESP-12F1.GPIO4
  N9: R3.Pin_0, WiFi-Witty-Gizwits-ESP-12F1.RXD, J1.pin3
  N10: R5.Pin_0, WiFi-Witty-Gizwits-ESP-12F1.GPIO14
  N11: R5.Pin_1, Q5.B
  5V: D4.cathode, 12V.pin2, C2.+, R6.Pin_0, D5.cathode, U10.input_voltage, U10.output_voltage, C4.+, C5.+, K1.COIL2, K2.COIL2, 5V_GND_RGB_LED_e_Racão.pin6, IC1.IN
  N12: D4.anode, Q5.C, K2.COIL1
  3.3V: C3.+, WiFi-Witty-Gizwits-ESP-12F1.CH_PD, WiFi-Witty-Gizwits-ESP-12F1.VCC, IC1.OUT
  N13: R6.Pin_1, WiFi-Witty-Gizwits-ESP-12F1.GPIO12, DS18B20_e_PIR.pin2
  N14: Relay1.pin1, K2.C
  N15: Relay1.pin2, K2.B
  N16: Relay2.pin1, K1.C
  N17: Relay2.pin2, K1.B
  N18: R7.Pin_0, WiFi-Witty-Gizwits-ESP-12F1.GPIO16
  N19: R7.Pin_1, Q6.B
  N20: D5.anode, Q6.C, K1.COIL1
  N21: WiFi-Witty-Gizwits-ESP-12F1.GPIO13, DS18B20_e_PIR.pin1
  N22: WiFi-Witty-Gizwits-ESP-12F1.GPIO15, R8.Pin_0, J1.pin2
  N23: WiFi-Witty-Gizwits-ESP-12F1.TXD, J1.pin4
  N24: Q7.B, R8.Pin_1
  N25: Q7.C, 5V_GND_RGB_LED_e_Racão.pin1

custom parts:
  WiFi-Witty-Gizwits-ESP-12F: A breadboard friendly two part WiFi development board by Gizwits, powered by an ESP8266 ESP-12F SoC, featuring twin micro-usb ports, a photoresistor, a WS2812 RGB-LED and three buttons. The board comes in two parts. The bottom half has reset and flash buttons, a micro-usb with CH340 UART and 2x 1x08 female headers. The top half has the ESP-12F, LDR, RGB-LED, micro-usb (for power only), an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
